# Fritzing sketch FAE089LIT22VMT8 (saved by Fritzing 0.9.2b)
circuit board: 8.46667cm x 5.64444cm

parts:
  BREAKOUT1 = HMC5883L Compass Breakout
  Onderdeel1 = Arduino Uno (Rev3) - ICSP

nets:
  N1: BREAKOUT1.SCL, Onderdeel1.A5/SCL
  N2: BREAKOUT1.SDA, Onderdeel1.A4/SDA
  GND: BREAKOUT1.GND, Onderdeel1.GND
  VIN: BREAKOUT1.VIN, Onderdeel1.5V

notes:
  Author: Danny van den Brande, Arduinosensors.nl
